# Fritzing sketch Arduino Leonardo Shield - Atari ST Keyboard 8Pin-18Pin-RJ11-Shield.REV0 (saved by Fritzing 0.9.5d)
circuit board: 6.88566cm x 5.36311cm
breadboards: 1

parts:
  Leonardo_Atari_Keyboard_Shield = Arduino Uno (Rev3)
  Atari_7_pin_KEYB = female pin header, 8 pins [form="♀ (female)"]
  RJ11 = RJ11 Jack [package=rj11-6]
  Atari_18_pin_Keyboard = female pin header, 18 pins [form="♀ (female)"]
  RJ11/7Pin = SPST Switch [package=switch-spdt_kit]
  9Pin-0 = DB9 Connector [package=db9]

nets:
  N1: Leonardo_Atari_Keyboard_Shield.D8, Atari_7_pin_KEYB.pin3
  N2: Leonardo_Atari_Keyboard_Shield.D9_PWM, Atari_7_pin_KEYB.pin7, Atari_18_pin_Keyboard.pin16
  N3: Leonardo_Atari_Keyboard_Shield.GND, Atari_7_pin_KEYB.pin1, RJ11.1, RJ11.2
  N4: Leonardo_Atari_Keyboard_Shield.D0/RX, Atari_7_pin_KEYB.pin5, RJ11.3, Atari_18_pin_Keyboard.pin14
  N5: Leonardo_Atari_Keyboard_Shield.D1/TX, Atari_7_pin_KEYB.pin6, RJ11.4, Atari_18_pin_Keyboard.pin15
  N6: Leonardo_Atari_Keyboard_Shield.5V, Atari_18_pin_Keyboard.pin13, RJ11/7Pin.P, 9Pin-0.7
  N7: Atari_7_pin_KEYB.pin4, RJ11/7Pin.S
  N8: RJ11.5, RJ11.6, RJ11/7Pin.O
  N9: Atari_18_pin_Keyboard.pin8, 9Pin-0.4
  N10: Atari_18_pin_Keyboard.pin9, 9Pin-0.3
  N11: Atari_18_pin_Keyboard.pin10, 9Pin-0.2
  N12: Atari_18_pin_Keyboard.pin11, 9Pin-0.6
  N13: Atari_18_pin_Keyboard.pin12, 9Pin-0.1
  N14: Atari_18_pin_Keyboard.pin17, 9Pin-0.9

notes:
  REV.0
  Mega ST(E)/TT
