# Fritzing sketch Arduino Leonardo Shield - Atari ST Keyboard 8Pin-18Pin-RJ11-Shield.REV1 (saved by Fritzing 0.9.5d)
circuit board: 6.88566cm x 5.36311cm
breadboards: 1

parts:
  Atari_7_pin_KEYB = female pin header, 8 pins [form="♀ (female)"]
  RJ11 = RJ11 Jack [package=rj11-6]
  Atari_18_pin_Keyboard = female pin header, 18 pins [form="♀ (female)"]
  Mouse/Keyb = SPST Switch [package=switch-spdt_kit]
  9Pin-0 = DB9 Connector [package=db9]
  C1 = Electrolytic Capacitor [capacitance=1µF package="100 mil [THT, electrolytic]"]
  Leonardo_Atari_Keyboard_Shield = Arduino Uno (Rev3)
  RJ11/7Pin = SPST Switch [package=switch-spdt_kit]

nets:
  N1: Atari_7_pin_KEYB.pin1, RJ11.1, RJ11.2, Mouse/Keyb.O, C1.-, Leonardo_Atari_Keyboard_Shield.GND
  N2: Atari_7_pin_KEYB.pin3, Leonardo_Atari_Keyboard_Shield.D8
  N3: Atari_7_pin_KEYB.pin4, Atari_18_pin_Keyboard.pin13, 9Pin-0.7, RJ11/7Pin.S
  N4: Atari_7_pin_KEYB.pin5, RJ11.3, Atari_18_pin_Keyboard.pin14, Leonardo_Atari_Keyboard_Shield.D0/RX
  N5: Atari_7_pin_KEYB.pin6, RJ11.4, Atari_18_pin_Keyboard.pin15, Leonardo_Atari_Keyboard_Shield.D1/TX
  N6: Atari_7_pin_KEYB.pin7, Atari_18_pin_Keyboard.pin16, Leonardo_Atari_Keyboard_Shield.D9_PWM
  N7: RJ11.5, RJ11.6, Mouse/Keyb.S, RJ11/7Pin.O
  N8: Atari_18_pin_Keyboard.pin8, 9Pin-0.4
  N9: Atari_18_pin_Keyboard.pin9, 9Pin-0.3
  N10: Atari_18_pin_Keyboard.pin10, 9Pin-0.2
  N11: Atari_18_pin_Keyboard.pin11, 9Pin-0.6
  N12: Atari_18_pin_Keyboard.pin12, 9Pin-0.1
  N13: Atari_18_pin_Keyboard.pin17, 9Pin-0.9
  N14: Mouse/Keyb.P, Leonardo_Atari_Keyboard_Shield.D2
  N15: C1.+, Leonardo_Atari_Keyboard_Shield.5V, RJ11/7Pin.P

notes:
  REV.1
  Mega ST(E)/TT
