# Fritzing sketch Atari ST(E)_MegaST_MegaSTE_TT_Falcon_Keyboard-To-Arduino_Micro_REV2 (saved by Fritzing 0.9.5d)
circuit board: 3.68cm x 4.83351cm
breadboards: 1

parts:
  Arduino_Micro = Arduino Micro (Rev3)
  RJ11 = RJ11 Jack [package=rj11-6]
  Atari_7_pin_KEYB = female pin header, 7 pins [form="♀ (female)"]

nets:
  N1: Arduino_Micro.D1/TX, RJ11.3, Atari_7_pin_KEYB.pin5
  N2: Arduino_Micro.D0/RX, RJ11.4, Atari_7_pin_KEYB.pin6
  N3: Arduino_Micro.GND, RJ11.5, RJ11.6, Atari_7_pin_KEYB.pin1
  N4: Arduino_Micro.D10_PWM/A10, Atari_7_pin_KEYB.pin7
  N5: Arduino_Micro.5V, RJ11.1, RJ11.2, Atari_7_pin_KEYB.pin4
  N6: Arduino_Micro.A0, Atari_7_pin_KEYB.pin3

notes:
  ATMega32U4
  USB
