# Fritzing sketch Atari ST(E)_MegaST_MegaSTE_TT_Falcon_Keyboard-To-Arduino_Micro_REV7 (saved by Fritzing 0.9.5d)
circuit board: 4.02cm x 4.95cm
breadboards: 1

parts:
  Arduino_Micro = Arduino Micro (Rev3)
  RJ11 = RJ11 Jack [package=rj11-6]
  Atari_7_pin_KEYB = female pin header, 8 pins [form="♀ (female)"]
  SW1 = female pin header, 3 pins [form="♀ (female)"]
  C1 = Electrolytic Capacitor [capacitance=100µF voltage=16V package="100 mil [THT, electrolytic]"]

nets:
  N1: Arduino_Micro.D1/TX, RJ11.4, Atari_7_pin_KEYB.pin6
  N2: Arduino_Micro.D0/RX, RJ11.3, Atari_7_pin_KEYB.pin5
  N3: Arduino_Micro.GND, RJ11.1, RJ11.2, Atari_7_pin_KEYB.pin1, SW1.pin1, C1.-
  N4: Arduino_Micro.D2/SDA, SW1.pin2
  N5: Arduino_Micro.D8_PWM/A8, Atari_7_pin_KEYB.pin3
  N6: Arduino_Micro.D9_PWM/A9, Atari_7_pin_KEYB.pin7
  N7: Arduino_Micro.5V, RJ11.5, RJ11.6, Atari_7_pin_KEYB.pin4, SW1.pin3, C1.+

notes:
  ATMega32U4
  USB
  Atari ST
  Rev.7
  Mega ST
  STE / Mega STE
  STm / STf / STFM
  TT / Falcon
  Keyboard to USB
  Supports:
  M.Farrell © 2021
