# Fritzing sketch Atari ST(E)_MegaST_MegaSTE_TT_Falcon_Keyboard-To-Arduino_ProMicro_REV0 (saved by Fritzing 0.9.5d)
circuit board: 3.58cm x 3.33cm
breadboards: 1

parts:
  Arduino_Pro_Micro = Arduino Micro (Rev3)
  RJ11 = RJ11 Jack [package=rj11-6]
  Atari_Int_Keyb = female pin header, 7 pins [form="♀ (female)"]

nets:
  N1: Arduino_Pro_Micro.D1/TX, RJ11.3, Atari_Int_Keyb.pin5
  N2: Arduino_Pro_Micro.D0/RX, RJ11.4, Atari_Int_Keyb.pin6
  N3: Arduino_Pro_Micro.GND, RJ11.5, RJ11.6, Atari_Int_Keyb.pin1
  N4: Arduino_Pro_Micro.5V, RJ11.1, RJ11.2, Atari_Int_Keyb.pin4

notes:
  ATMega32U4
  USB
