# Fritzing sketch Atari ST(E)_MegaST_MegaSTE_TT_Falcon_Keyboard-To-Arduino_ProMicro_REV1 (saved by Fritzing 0.9.5d)
circuit board: 3.58cm x 3.33cm
breadboards: 1

parts:
  RJ11 = RJ11 Jack [package=rj11-6]
  Atari_Internal = female pin header, 1 pin [form="♀ (female)"]
  Keyboard_7Pin = female pin header, 5 pins [form="♀ (female)"]
  Pro_Micro1 = SparkFun Pro Micro

nets:
  N1: RJ11.1, RJ11.2, Atari_Internal.pin1, Keyboard_7Pin.pin2, Pro_Micro1.VCC
  N2: RJ11.3, Keyboard_7Pin.pin3, Pro_Micro1.TX0
  N3: RJ11.4, Keyboard_7Pin.pin4, Pro_Micro1.RX1
  N4: RJ11.5, RJ11.6, Pro_Micro1.GND
  N5: Keyboard_7Pin.pin1, Pro_Micro1.A0
  N6: Keyboard_7Pin.pin5, Pro_Micro1.10

notes:
  ATMega32U4
  USB

custom parts:
  SparkFun Pro Micro: The Pro Micro is similar to the Pro Mini except with an ATmega32U4 on board. The USB transceiver inside the 32U4 allows us to add USB connectivity on-board and do away with bulky external USB interface. Based on: https://github.com/unorthodox-engineers/unorthodox-arduino/blob/master/Unorthodox/fritzing/parts/Pro%20Micro.fzpz
