# Fritzing sketch Atari ST(E)_MegaST_MegaSTE_TT_Falcon_Keyboard-To-Arduino_ProMicro_REV3 (saved by Fritzing 0.9.5d)
circuit board: 3.58cm x 3.33cm
breadboards: 1

parts:
  RJ11 = RJ11 Jack [package=rj11-6]
  Atari_ST_KEYB = female pin header, 1 pin [form="♀ (female)"]
  7pin = female pin header, 5 pins [form="♀ (female)"]
  Pro_Micro = SparkFun Pro Micro

nets:
  N1: RJ11.1, RJ11.2, Atari_ST_KEYB.pin1, Pro_Micro.GND
  N2: RJ11.3, 7pin.pin3, Pro_Micro.RX1
  N3: RJ11.4, 7pin.pin4, Pro_Micro.TX0
  N4: RJ11.5, RJ11.6, 7pin.pin2, Pro_Micro.VCC
  N5: 7pin.pin1, Pro_Micro.A0
  N6: 7pin.pin5, Pro_Micro.10

notes:
  ATMega32U4
  USB

custom parts:
  SparkFun Pro Micro: The Pro Micro is similar to the Pro Mini except with an ATmega32U4 on board. The USB transceiver inside the 32U4 allows us to add USB connectivity on-board and do away with bulky external USB interface. Based on: https://github.com/unorthodox-engineers/unorthodox-arduino/blob/master/Unorthodox/fritzing/parts/Pro%20Micro.fzpz
